# Fritzing sketch schematic-attiny (saved by Fritzing 0.9.6b)
breadboards: 1

parts:
  Receiver = IC, SIP package, 8 pins [chip_label=RX]
  2S_Lipo = DC Power [voltage=8.4V]
  J1 = Basic Servo
  J2 = Basic Servo
  Diode = Rectifier Diode 10A [part_number=P1000K]
  IC1 = IC, DIP package, 10 pins [chip_label=ATTiny85]

nets:
  N1: Receiver.pin1, IC1.pin3
  N2: Receiver.pin2, IC1.pin1
  N3: Receiver.pin3, IC1.pin10
  N4: Receiver.pin4, IC1.pin9
  N5: Receiver.pin5, IC1.pin8
  VCC: 2S_Lipo.V+, J1.vcc, J2.vcc, Diode.anode
  GND: 2S_Lipo.V-, J1.gnd, J2.gnd
  N6: J1.pulse, IC1.pin7
  N7: J2.pulse, IC1.pin6
  N8: Diode.cathode, IC1.pin2
