# Fritzing sketch schematic-nano (saved by Fritzing 0.9.3b)
breadboards: 1

parts:
  Receiver = IC, SIP package, 8 pins [chip_label=RX]
  Nano1 = Arduino Nano v2.3
  2S_Lipo = DC Power [voltage=8.4V]
  J1 = Basic Servo
  J2 = Basic Servo
  Diode = Rectifier Diode 10A
  R1 = Resistor [tolerance=±5% resistance=100k package="0805 [SMD]"]
  R2 = Resistor [tolerance=±5% resistance=147k package="0805 [SMD]"]

nets:
  GND: Receiver.pin1, Nano1.GND, 2S_Lipo.V-, J1.gnd, J2.gnd, R2.Pin_1
  N1: Receiver.pin2, Nano1.+5V
  N2: Receiver.pin3, Nano1.D9
  N3: Receiver.pin4, Nano1.D10
  N4: Receiver.pin5, Nano1.D11
  N5: Receiver.pin6, Nano1.D12
  N6: Nano1.D2, J2.pulse
  N7: Nano1.D3, J1.pulse
  N8: Nano1.A7, R1.Pin_1, R2.Pin_0
  N9: Nano1.VIN, Diode.cathode, R1.Pin_0
  VCC: 2S_Lipo.V+, J1.vcc, J2.vcc, Diode.anode
